// Logisim project Parkovisko.circ as structural Verilog: 1 circuit, main circuit main
module main (
  input  S,
  input  R,
  input  A,
  input  B,
  input  C
);

  wire and_1_out, and_2_out, and_3_out, clock_1_out, counter_1_carry, counter_2_carry, counter_3_carry,
       j_k_ff_1_q, j_k_ff_1_qn, j_k_ff_2_q, j_k_ff_2_qn, nand_1_out, nand_2_out, nand_3_out, nand_4_out,
       nand_5_out, nand_6_out, nand_7_out, nand_8_out, nand_9_out, nand_10_out, nand_11_out, nand_12_out,
       nand_13_out, nor_1_out, nor_2_out, nor_3_out, not_1_out, not_2_out, not_3_out, not_4_out, not_5_out,
       not_6_out, not_7_out, not_8_out, not_9_out, not_10_out, not_11_out, not_12_out, not_13_out,
       not_14_out, not_15_out;
  wire [3:0] counter_1_q, counter_2_q, counter_3_q;

  Clock clock_1 (.out(clock_1_out));
  not not_1 (not_1_out, A);
  not not_2 (not_2_out, B);
  not not_3 (not_3_out, C);
  nand nand_1 (nand_1_out, j_k_ff_2_q, not_1_out, not_2_out, not_3_out);
  nand nand_2 (nand_2_out, j_k_ff_2_qn, not_1_out, not_2_out, C);
  nand nand_3 (nand_3_out, j_k_ff_1_q, j_k_ff_2_qn, A, not_2_out, not_3_out);
  and and_1 (and_1_out, A, B, C);
  nand nand_4 (nand_4_out, nand_1_out, nand_2_out, nand_3_out);
  and and_2 (and_2_out, j_k_ff_1_qn, A, not_2_out, C);
  and and_3 (and_3_out, j_k_ff_1_qn, not_1_out, not_2_out, not_3_out);
  nand nand_5 (nand_5_out, j_k_ff_1_qn, j_k_ff_2_q, not_1_out, not_2_out, C);
  not not_4 (not_4_out, nand_5_out);
  nand nand_6 (nand_6_out, j_k_ff_1_qn, j_k_ff_2_q, A, not_2_out, not_3_out);
  not not_5 (not_5_out, nand_6_out);
  not not_6 (not_6_out, nand_7_out);
  nand nand_7 (nand_7_out, j_k_ff_1_q, j_k_ff_2_qn, not_1_out, B, C);
  nand nand_8 (nand_8_out, j_k_ff_1_q, j_k_ff_2_qn, A, B, not_3_out);
  not not_7 (not_7_out, nand_8_out);
  not not_8 (not_8_out, nand_9_out);
  nand nand_9 (nand_9_out, j_k_ff_1_q, j_k_ff_2_q, not_1_out, not_2_out, C);
  not not_9 (not_9_out, nand_10_out);
  nand nand_10 (nand_10_out, j_k_ff_1_q, j_k_ff_2_q, A, not_2_out, not_3_out);
  J_K_Flip_Flop j_k_ff_1 (
    .J(and_1_out), .clk(clock_1_out), .K(nand_4_out), .Q(j_k_ff_1_q), .Qn(j_k_ff_1_qn), .preset(S), .reset(R));  // open: en
  J_K_Flip_Flop j_k_ff_2 (
    .J(and_2_out), .clk(clock_1_out), .K(and_3_out), .Q(j_k_ff_2_q), .Qn(j_k_ff_2_qn), .preset(S), .reset(R));  // open: en
  nor nor_1 (nor_1_out, not_4_out, not_5_out);
  nor nor_2 (nor_2_out, not_6_out, not_7_out);
  nor nor_3 (nor_3_out, not_8_out, not_9_out);
  LED A_plus (.in(not_4_out));
  LED A_minus (.in(not_5_out));
  not not_10 (not_10_out, nor_1_out);
  not not_11 (not_11_out, nor_2_out);
  not not_12 (not_12_out, nor_3_out);
  LED B_plus (.in(not_6_out));
  LED D_minus (.in(not_9_out));
  LED D_plus (.in(not_8_out));
  LED B_minus (.in(not_7_out));
  Counter #(.width(4), .max('h4), .ongoal("stay")) counter_1 (
    .load(not_5_out), .Q(counter_1_q), .carry(counter_1_carry), .clk(not_10_out), .clr(R));  // open: D, count
  not not_13 (not_13_out, not_5_out);
  Counter #(.width(4), .max('h2), .ongoal("stay")) counter_2 (
    .load(not_7_out), .Q(counter_2_q), .carry(counter_2_carry), .clk(not_11_out), .clr(R));  // open: D, count
  not not_14 (not_14_out, not_7_out);
  Counter #(.width(4), .max('h3), .ongoal("stay")) counter_3 (
    .load(not_9_out), .Q(counter_3_q), .carry(counter_3_carry), .clk(not_12_out), .clr(R));  // open: D, count
  nand nand_11 (nand_11_out, counter_1_carry, not_13_out);
  nand nand_12 (nand_12_out, counter_2_carry, not_14_out);
  nand nand_13 (nand_13_out, counter_3_carry, not_15_out);
  not not_15 (not_15_out, not_9_out);
  LED Auta (.in(nand_11_out));
  Hex_Digit_Display hex_digit_display_1 (.value(counter_1_q));  // open: dp
  LED Autobusy (.in(nand_12_out));
  Hex_Digit_Display hex_digit_display_2 (.value(counter_2_q));  // open: dp
  LED Dodavky (.in(nand_13_out));
  Hex_Digit_Display hex_digit_display_3 (.value(counter_3_q));  // open: dp

  // Notes on the sheet:
  //   Z1
  //   Z2
endmodule
